# Fritzing sketch robo l298 (saved by Fritzing 0.9.3b)
breadboards: 1

parts:
  Componente2 = Photon
  S1 = H-Bridge with L298N
  M3 = DC Motor
  M4 = DC Motor

nets:
  N1: Componente2.A0, S1.ENA, S1.IN1
  N2: Componente2.A1, S1.IN2
  N3: Componente2.A2, Componente2.A3, S1.IN3, S1.IN4
  GND: Componente2.GND, S1.GND
  VIN: Componente2.VIN, S1.5V
  N4: S1.M1-01, M3.pin_2
  N5: S1.M1-02, M3.pin_1
  N6: S1.M2-01, M4.pin_2
  N7: S1.M2-02, M4.pin_1

custom parts:
  H-Bridge with L298N: h-bridge
